# Fritzing sketch TX_Schematic (saved by Fritzing 0.9.3b)
perfboards: 1

parts:
  S2 = Toggle Switch [package=THT]
  TrimPCF = PCF8574 [package="DIP16 [THT]"]
  S3 = Pushbutton [package=THT]
  S4 = Pushbutton [package=THT]
  S5 = Pushbutton [package=THT]
  S6 = Pushbutton [package=THT]
  S7 = Pushbutton [package=THT]
  S8 = Pushbutton [package=THT]
  S9 = Pushbutton [package=THT]
  S10 = Pushbutton [package=THT]
  R-Joystick = Thumb Joystick [package=joystick]
  Button/Switch_PCF = PCF8574 [package="DIP16 [THT]"]
  S12 = Pushbutton [package=THT]
  S13 = Pushbutton [package=THT]
  S14 = Pushbutton [package=THT]
  S15 = Pushbutton [package=THT]
  S16 = Pushbutton [package=THT]
  S17 = Pushbutton [package=THT]
  R2 = Resistor [tolerance=±5% resistance=4.7k package=THT]
  R3 = Resistor [tolerance=±5% resistance=4.7k package=THT]
  Part2 = NRF24L01+ Breakout Board
  L-Joystick = Thumb Joystick [package=joystick]
  buzzer = Piezo Speaker
  U1 = LIPO-1000mAh [package=lipo-1000]
  Part1 = Arduino Pro Mini (5V)
  LED1 = LED - 5mm [color="Red (633nm)" package="5 mm [THT]"]
  LEDBlue = LED - 5mm [color="Blue (525nm)" package="5 mm [THT]"]
  R4 = Resistor [tolerance=±1% resistance=10k package=THT]
  S20 = Toggle Switch [package=THT]
  Part3 = Taiway 100-SP-X-T1 SPDT Miniature Toggle Switch [part_number=100-SP-X-T1-0-0-B1-M1 package=THT]  # not connected
  S21 = Taiway 100-SP-X-T1 SPDT Miniature Toggle Switch [part_number="on off on" package=THT]
  TP4056-Protect_+_booster = IC, DIP package, 4 pins [chip_label=IC]

nets:
  N1: S2.COM, TP4056-Protect_+_booster.pin3
  VCC: S2.L2, R-Joystick.V+, R-Joystick.H+, Part2.VCC, L-Joystick.V+, L-Joystick.H+, Part1.VCC, LED1.anode, LEDBlue.anode, S21.L2
  GND: TrimPCF.A0, TrimPCF.A1, TrimPCF.A3, Button/Switch_PCF.A0, Button/Switch_PCF.A1, Button/Switch_PCF.GND, S12.leg1, S13.leg1, S14.leg0, S15.leg1, S16.leg1, S17.leg0, Part2.GND, S20.COM
  N2: TrimPCF.P0, S3.leg1
  N3: TrimPCF.P1, S4.leg1
  N4: TrimPCF.P2, S5.leg1
  N5: TrimPCF.P3, S6.leg1
  GND_2: TrimPCF.GND, S3.leg0, S4.leg0, S5.leg0, S6.leg0, S7.leg1, S8.leg1, S9.leg1, S10.leg1, R-Joystick.H-, R-Joystick.V-, L-Joystick.H-, L-Joystick.V-, buzzer.pin2, Part1.GND, R4.Pin_0, TP4056-Protect_+_booster.pin2
  N6: TrimPCF.P4, S7.leg0
  N7: TrimPCF.P5, S8.leg0
  N8: TrimPCF.P6, S9.leg0
  N9: TrimPCF.P7, S10.leg0
  N10: TrimPCF.INT, Button/Switch_PCF.INT, Part1.D2
  N11: TrimPCF.SCL, Button/Switch_PCF.SCL, R2.Pin_1, Part1.A5
  N12: TrimPCF.SDA, Button/Switch_PCF.SDA, R3.Pin_1, Part1.A4
  5V: TrimPCF.VCC, Button/Switch_PCF.A3, Button/Switch_PCF.VCC, R2.Pin_0, R3.Pin_0
  N13: R-Joystick.V, Part1.A2
  N14: R-Joystick.H, Part1.A3
  N15: Button/Switch_PCF.P0, S20.L1
  N16: Button/Switch_PCF.P1, S20.L2
  N17: Button/Switch_PCF.P2, S14.leg1
  N18: Button/Switch_PCF.P3, S17.leg1
  N19: Button/Switch_PCF.P4, S13.leg0
  N20: Button/Switch_PCF.P5, S16.leg0
  N21: Button/Switch_PCF.P6, S12.leg0
  N22: Button/Switch_PCF.P7, S15.leg0
  N23: Part2.CE, Part1.D7
  N24: Part2.CS, Part1.D9
  N25: Part2.SCK, Part1.SCK
  N26: Part2.MOSI, Part1.MOSI
  N27: Part2.MISO, Part1.MISO
  N28: L-Joystick.V, Part1.A0
  N29: L-Joystick.H, Part1.A1
  N30: buzzer.pin1, Part1.D8
  N31: U1.+, Part1.A6, TP4056-Protect_+_booster.pin4
  N32: U1.-, TP4056-Protect_+_booster.pin1
  N33: Part1.A7, R4.Pin_1, S21.COM
  N34: Part1.D6, LED1.cathode
  N35: Part1.D5, LEDBlue.cathode
  3.3V: S21.L1
